// Logisim project BCD.circ as structural Verilog: 1 circuit, main circuit 5位2进制转BCD
module \_5位2进制转BCD  (
  input  in_1,
  input  I3,
  input  I2,
  input  I1,
  input  I0,
  output S7,
  output S6,
  output S5,
  output S4,
  output S3,
  output S2,
  output S1,
  output S0
);

  wire and_3_out, or_1_out, or_2_out, or_3_out, or_4_out;

  and and_1 (S5, in_1, or_2_out);
  and and_2 (S4, ~S5, or_1_out);  // AND_Gate
  or or_1 (or_1_out, in_1, and_3_out);
  or or_2 (or_2_out, I3, I2);
  or or_3 (or_3_out, S5, S4);
  // 四位二进制并行加法器 四位二进制并行加法器_1: pin names not known; wires that end beside it: I3, S3, I2, I1, S2, I0, S5, S1, or_3_out, S4, S0, 1'b0, 1'b0
  and and_3 (and_3_out, I3, or_4_out);
  or or_4 (or_4_out, I2, I1);

  assign S6 = 1'b0;
  assign S7 = 1'b0;
endmodule
