// Logisim project counter.circ as structural Verilog: 1 circuit, main circuit 24s 8s 3s计时器
module \_24s_8s_3s计时器  (
  input  S24,
  input  CLR,
  input  M,
  input  S8,
  input  CLR8,
  input  S3,
  input  CLR3,
  input  clk,
  output SA,
  output SB,
  output SC,
  output SD,
  output SE,
  output SA8,
  output SB8,
  output SC8,
  output SA3,
  output SB3
);

  wire and_1_out, and_2_out, and_3_out, d_ff_1_qn, d_ff_2_qn, d_ff_3_qn, d_ff_4_qn, d_ff_5_qn, d_ff_6_qn,
       d_ff_7_qn, d_ff_8_qn, d_ff_9_qn, d_ff_10_qn, xor_1_out, xor_2_out, xor_3_out, xor_4_out, xor_5_out,
       xor_6_out, xor_7_out;

  and and_1 (and_1_out, S24, clk);
  D_Flip_Flop d_ff_1 (.clk(and_1_out), .D(d_ff_1_qn), .Q(SA), .Qn(d_ff_1_qn), .reset(CLR));  // open: preset, en
  xor xor_1 (xor_1_out, d_ff_1_qn, M);
  D_Flip_Flop d_ff_2 (.clk(xor_1_out), .D(d_ff_2_qn), .Q(SB), .Qn(d_ff_2_qn), .reset(CLR));  // open: preset, en
  xor xor_2 (xor_2_out, d_ff_2_qn, M);
  D_Flip_Flop d_ff_3 (.clk(xor_2_out), .D(d_ff_3_qn), .Q(SC), .Qn(d_ff_3_qn), .reset(CLR));  // open: preset, en
  xor xor_3 (xor_3_out, d_ff_3_qn, M);
  D_Flip_Flop d_ff_4 (.clk(xor_3_out), .D(d_ff_4_qn), .Q(SD), .Qn(d_ff_4_qn), .reset(CLR));  // open: preset, en
  xor xor_4 (xor_4_out, d_ff_4_qn, M);
  D_Flip_Flop d_ff_5 (.clk(xor_4_out), .D(d_ff_5_qn), .Q(SE), .Qn(d_ff_5_qn), .reset(CLR));  // open: preset, en
  and and_2 (and_2_out, S8, clk);
  D_Flip_Flop d_ff_6 (.clk(and_2_out), .D(d_ff_6_qn), .Q(SA8), .Qn(d_ff_6_qn), .reset(CLR8));  // open: preset, en
  xor xor_5 (xor_5_out, d_ff_6_qn, M);
  D_Flip_Flop d_ff_7 (.clk(xor_5_out), .D(d_ff_7_qn), .Q(SB8), .Qn(d_ff_7_qn), .reset(CLR8));  // open: preset, en
  xor xor_6 (xor_6_out, d_ff_7_qn, M);
  D_Flip_Flop d_ff_8 (.clk(xor_6_out), .D(d_ff_8_qn), .Q(SC8), .Qn(d_ff_8_qn), .reset(CLR8));  // open: preset, en
  and and_3 (and_3_out, S3, clk);
  D_Flip_Flop d_ff_9 (.clk(and_3_out), .D(d_ff_9_qn), .Q(SA3), .Qn(d_ff_9_qn), .reset(CLR3));  // open: preset, en
  xor xor_7 (xor_7_out, d_ff_9_qn, M);
  D_Flip_Flop d_ff_10 (.clk(xor_7_out), .D(d_ff_10_qn), .Q(SB3), .Qn(d_ff_10_qn), .reset(CLR3));  // open: preset, en
endmodule
