// Logisim project design.circ as structural Verilog: 1 circuit, main circuit main
module main (
  input  \_24s开始计时 ,
  input  in_2,
  input  \_7s开始计时 ,
  input  \_3s开始计时 ,
  input  \暂停_播放音乐 ,
  input  in_6,
  output a,
  output b,
  output c,
  output d,
  output e,
  output f,
  output g,
  output a_2,
  output b_2,
  output c_2,
  output d_2,
  output e_2,
  output f_2,
  output g_2,
  output a_3,
  output b_3,
  output c_3,
  output d_3,
  output e_3,
  output f_3,
  output g_3,
  output a_4,
  output b_4,
  output c_4,
  output d_4,
  output e_4,
  output f_4,
  output g_4,
  output a_5,
  output b_5,
  output c_5,
  output d_5,
  output e_5,
  output f_5,
  output g_5
);

  wire \_3s清零_out , \_7s清零_out , \_24s清零_out , and_1_out, and_2_out, and_3_out, clock_1_out, clock_2_out,
       \n5位2进制转bcd_1_s0 , \n5位2进制转bcd_1_s1 , \n5位2进制转bcd_1_s2 , \n5位2进制转bcd_1_s3 , \n5位2进制转bcd_1_s4 ,
       \n5位2进制转bcd_1_s5 , \n5位2进制转bcd_1_s6 , \n5位2进制转bcd_1_s7 , \n5位2进制转bcd_2_s0 , \n5位2进制转bcd_2_s1 ,
       \n5位2进制转bcd_2_s2 , \n5位2进制转bcd_2_s3 , \n5位2进制转bcd_3_s0 , \n5位2进制转bcd_3_s1 , \n5位2进制转bcd_3_s2 ,
       \n5位2进制转bcd_3_s3 , \n24s_8s_3s计时器_1_sa , \n24s_8s_3s计时器_1_sa3 , \n24s_8s_3s计时器_1_sa8 ,
       \n24s_8s_3s计时器_1_sb , \n24s_8s_3s计时器_1_sb3 , \n24s_8s_3s计时器_1_sb8 , \n24s_8s_3s计时器_1_sc ,
       \n24s_8s_3s计时器_1_sc8 , \n24s_8s_3s计时器_1_sd , \n24s_8s_3s计时器_1_se , \n24s_8s_3s计时器_2_sa ,
       \n24s_8s_3s计时器_2_sb , \n24s_8s_3s计时器_2_sc , \n24s_8s_3s计时器_2_sd , \n24s_8s_3s计时器_2_se , nand_1_out,
       nand_2_out, nand_3_out, not_1_out, \重头播放_out , \音乐播放器_1_out_6 , \音乐播放器_1_out_7 , \音乐播放器_1_out_8 ,
       \音乐播放器_1_out_9 ;

  LED #(.active("false")) \_24s违例  (.in(nand_1_out));
  LED #(.active("false")) \u_半场警告  (.in(nand_2_out));
  Button \_24s清零  (.out(\_24s清零_out ));
  Button \_7s清零  (.out(\_7s清零_out ));
  Button \_3s清零  (.out(\_3s清零_out ));
  Button \u_重头播放  (.out(\重头播放_out ));
  LED #(.active("false")) \_3s违例  (.in(nand_3_out));
  nand nand_1 (nand_1_out, \n24s_8s_3s计时器_1_se , \n24s_8s_3s计时器_1_sd );
  not not_1 (not_1_out, \暂停_播放音乐 );
  exp2_3_lib_main main_1 (
    .A3(\n5位2进制转bcd_1_s7 ), .A2(\n5位2进制转bcd_1_s6 ), .A1(\n5位2进制转bcd_1_s5 ), .A0(\n5位2进制转bcd_1_s4 ), .Fa(a),
    .Fb(b), .Fc(c), .Fd(d), .Fe(e), .Ff(f), .Fg(g));
  nand nand_2 (nand_2_out, \n24s_8s_3s计时器_1_sc8 , \n24s_8s_3s计时器_1_sb8 , \n24s_8s_3s计时器_1_sa8 );
  nand nand_3 (nand_3_out, \n24s_8s_3s计时器_1_sb3 , \n24s_8s_3s计时器_1_sa3 );
  and and_1 (and_1_out, nand_1_out, not_1_out, \_24s开始计时 );
  and and_2 (and_2_out, nand_2_out, not_1_out, \_7s开始计时 );
  and and_3 (and_3_out, nand_3_out, not_1_out, \_3s开始计时 );
  _7_Segment_Display u_7_segment_display_1 (.g(g), .f(f), .a(a), .b(b), .e(e), .d(d), .c(c));  // open: dp
  exp2_3_lib_main main_2 (
    .A3(\n5位2进制转bcd_1_s3 ), .A2(\n5位2进制转bcd_1_s2 ), .A1(\n5位2进制转bcd_1_s1 ), .A0(\n5位2进制转bcd_1_s0 ), .Fa(a_2),
    .Fb(b_2), .Fc(c_2), .Fd(d_2), .Fe(e_2), .Ff(f_2), .Fg(g_2));
  \_5位2进制转BCD  \u_5位2进制转bcd_1  (
    .S7(\n5位2进制转bcd_1_s7 ), .S6(\n5位2进制转bcd_1_s6 ), .S5(\n5位2进制转bcd_1_s5 ), .S4(\n5位2进制转bcd_1_s4 ),
    .S3(\n5位2进制转bcd_1_s3 ), .S2(\n5位2进制转bcd_1_s2 ), .S1(\n5位2进制转bcd_1_s1 ), .S0(\n5位2进制转bcd_1_s0 ),
    .in_1(\n24s_8s_3s计时器_1_se ), .I3(\n24s_8s_3s计时器_1_sd ), .I2(\n24s_8s_3s计时器_1_sc ),
    .I1(\n24s_8s_3s计时器_1_sb ), .I0(\n24s_8s_3s计时器_1_sa ));
  _7_Segment_Display u_7_segment_display_2 (.g(g_2), .f(f_2), .a(a_2), .b(b_2), .e(e_2), .d(d_2), .c(c_2));  // open: dp
  \_24s_8s_3s计时器  \u_24s_8s_3s计时器_1  (
    .S24(and_1_out), .CLR(\_24s清零_out ), .M(in_2), .S8(and_2_out), .CLR8(\_7s清零_out ), .S3(and_3_out),
    .CLR3(\_3s清零_out ), .SA(\n24s_8s_3s计时器_1_sa ), .SB(\n24s_8s_3s计时器_1_sb ), .SC(\n24s_8s_3s计时器_1_sc ),
    .SD(\n24s_8s_3s计时器_1_sd ), .SE(\n24s_8s_3s计时器_1_se ), .SA8(\n24s_8s_3s计时器_1_sa8 ),
    .SB8(\n24s_8s_3s计时器_1_sb8 ), .SC8(\n24s_8s_3s计时器_1_sc8 ), .SA3(\n24s_8s_3s计时器_1_sa3 ),
    .SB3(\n24s_8s_3s计时器_1_sb3 ), .clk(clock_1_out));
  Clock clock_1 (.out(clock_1_out));
  \_24s_8s_3s计时器  \u_24s_8s_3s计时器_2  (
    .S24(\暂停_播放音乐 ), .CLR(\重头播放_out ), .M(in_6), .SA(\n24s_8s_3s计时器_2_sa ), .SB(\n24s_8s_3s计时器_2_sb ),
    .SC(\n24s_8s_3s计时器_2_sc ), .SD(\n24s_8s_3s计时器_2_sd ), .SE(\n24s_8s_3s计时器_2_se ), .clk(clock_2_out));  // open: S8, CLR8, S3, CLR3, SA8, SB8, SC8, SA3, SB3
  Clock clock_2 (.out(clock_2_out));
  \_5位2进制转BCD  \u_5位2进制转bcd_2  (
    .S3(\n5位2进制转bcd_2_s3 ), .S2(\n5位2进制转bcd_2_s2 ), .S1(\n5位2进制转bcd_2_s1 ), .S0(\n5位2进制转bcd_2_s0 ),
    .in_1(1'b0), .I3(1'b0), .I2(\n24s_8s_3s计时器_1_sc8 ), .I1(\n24s_8s_3s计时器_1_sb8 ), .I0(\n24s_8s_3s计时器_1_sa8 ));  // open: S7, S6, S5, S4
  _7_Segment_Display u_7_segment_display_3 (.g(g_3), .f(f_3), .a(a_3), .b(b_3), .e(e_3), .d(d_3), .c(c_3));  // open: dp
  exp2_3_lib_main main_3 (
    .A3(\n5位2进制转bcd_2_s3 ), .A2(\n5位2进制转bcd_2_s2 ), .A1(\n5位2进制转bcd_2_s1 ), .A0(\n5位2进制转bcd_2_s0 ), .Fa(a_3),
    .Fb(b_3), .Fc(c_3), .Fd(d_3), .Fe(e_3), .Ff(f_3), .Fg(g_3));
  exp2_3_lib_main main_4 (
    .A3(\n5位2进制转bcd_3_s3 ), .A2(\n5位2进制转bcd_3_s2 ), .A1(\n5位2进制转bcd_3_s1 ), .A0(\n5位2进制转bcd_3_s0 ), .Fa(a_4),
    .Fb(b_4), .Fc(c_4), .Fd(d_4), .Fe(e_4), .Ff(f_4), .Fg(g_4));
  \_5位2进制转BCD  \u_5位2进制转bcd_3  (
    .S3(\n5位2进制转bcd_3_s3 ), .S2(\n5位2进制转bcd_3_s2 ), .S1(\n5位2进制转bcd_3_s1 ), .S0(\n5位2进制转bcd_3_s0 ),
    .in_1(1'b0), .I3(1'b0), .I2(1'b0), .I1(\n24s_8s_3s计时器_1_sb3 ), .I0(\n24s_8s_3s计时器_1_sa3 ));  // open: S7, S6, S5, S4
  _7_Segment_Display u_7_segment_display_4 (.g(g_4), .f(f_4), .a(a_4), .b(b_4), .e(e_4), .d(d_4), .c(c_4));  // open: dp
  exp2_3_lib_main main_5 (
    .A3(\音乐播放器_1_out_9 ), .A2(\音乐播放器_1_out_8 ), .A1(\音乐播放器_1_out_7 ), .A0(\音乐播放器_1_out_6 ), .Fa(a_5),
    .Fb(b_5), .Fc(c_5), .Fd(d_5), .Fe(e_5), .Ff(f_5), .Fg(g_5));
  _7_Segment_Display u_7_segment_display_5 (.g(g_5), .f(f_5), .a(a_5), .b(b_5), .e(e_5), .d(d_5), .c(c_5));  // open: dp
  \音乐播放器  \u_音乐播放器_1  (
    .addr0(\n24s_8s_3s计时器_2_sa ), .addr1(\n24s_8s_3s计时器_2_sb ), .addr2(\n24s_8s_3s计时器_2_sc ),
    .addr3(\n24s_8s_3s计时器_2_sd ), .addr4(\n24s_8s_3s计时器_2_se ), .out_6(\音乐播放器_1_out_6 ),
    .out_7(\音乐播放器_1_out_7 ), .out_8(\音乐播放器_1_out_8 ), .out_9(\音乐播放器_1_out_9 ));
endmodule
