// Logisim project exp2_3_lib.circ as structural Verilog: 1 circuit, main circuit main
// 一位7段译码器
module main (
  input  A3,
  input  A2,
  input  A1,
  input  A0,
  output Fa,
  output Fb,
  output Fc,
  output Fd,
  output Fe,
  output Ff,
  output Fg
);

  wire and_1_out, and_2_out, and_3_out, and_4_out, and_5_out, and_6_out, and_7_out, and_8_out, and_9_out,
       and_10_out, and_11_out, and_12_out, and_13_out, and_14_out, and_15_out, and_16_out, and_17_out,
       and_18_out;

  and and_1 (and_1_out, ~A3, ~A2, ~A1, A0);  // AND_Gate
  and and_2 (and_2_out, ~A3, A2, ~A1, ~A0);  // AND_Gate
  and and_3 (and_3_out, ~A3, A2, ~A1, A0);  // AND_Gate
  and and_4 (and_4_out, ~A3, A2, A1, ~A0);  // AND_Gate
  nand nand_1 (Fc, ~A3, ~A2, A1, ~A0);  // NAND_Gate
  and and_5 (and_5_out, ~A3, ~A2, ~A1, A0);  // AND_Gate
  and and_6 (and_6_out, ~A3, A2, ~A1, ~A0);  // AND_Gate
  and and_7 (and_7_out, ~A3, A2, A1, A0);  // AND_Gate
  and and_8 (and_8_out, ~A3, ~A2, ~A1, ~A0);  // AND_Gate
  and and_9 (and_9_out, ~A3, ~A2, A1, ~A0);  // AND_Gate
  and and_10 (and_10_out, ~A3, A2, A1, ~A0);  // AND_Gate
  and and_11 (and_11_out, A3, ~A2, ~A1, ~A0);  // AND_Gate
  and and_12 (and_12_out, ~A3, ~A2, ~A1, A0);  // AND_Gate
  and and_13 (and_13_out, ~A3, ~A2, A1, ~A0);  // AND_Gate
  and and_14 (and_14_out, ~A3, ~A2, A1, A0);  // AND_Gate
  and and_15 (and_15_out, ~A3, A2, A1, A0);  // AND_Gate
  and and_16 (and_16_out, ~A3, ~A2, ~A1, ~A0);  // AND_Gate
  and and_17 (and_17_out, ~A3, ~A2, ~A1, A0);  // AND_Gate
  and and_18 (and_18_out, ~A3, A2, A1, A0);  // AND_Gate
  nor nor_1 (Fa, and_1_out, and_2_out);
  nor nor_2 (Fb, and_3_out, and_4_out);
  nor nor_3 (Fd, and_5_out, and_6_out, and_7_out);
  or or_1 (Fe, and_8_out, and_9_out, and_10_out, and_11_out);
  nor nor_4 (Ff, and_12_out, and_13_out, and_14_out, and_15_out);
  nor nor_5 (Fg, and_16_out, and_17_out, and_18_out);
endmodule
