// Logisim project music.circ as structural Verilog: 1 circuit, main circuit 音乐播放器
module \音乐播放器  (
  input  addr0,
  input  addr1,
  input  addr2,
  input  addr3,
  input  addr4,
  output out_6,
  output out_7,
  output out_8,
  output out_9
);

  wire undriven;

  ROM #(.addrWidth(5), .dataWidth(4)) rom_1 (
    .addr({addr4, addr3, addr2, addr1, addr0}), .data({out_9, out_8, out_7, out_6}), .sel(undriven));

  // Notes on the sheet:
  //   contents of rom_1 (hex, n*v repeats v):
  //   1 1 5 5 6 6 5 5 4 4 3 3 2 2 1 1 5 5 4 4 3 3 2 2 5 5 4 4 3 3 2 2
endmodule
