// Logisim project exp1_1.circ as structural Verilog: 1 circuit, main circuit main
module main (
  input  A,
  input  B,
  output S,
  output C
);

  xor xor_1 (S, A, B);
  and and_1 (C, A, B);

  // Notes on the sheet:
  //   S = A  XOR  B
  //   其中S是本位和，C是向高位的进位
  //   一位二进制半加器
  //   C=AB
endmodule
