// Logisim project exp1_3.circ as structural Verilog: 1 circuit, main circuit main
module main (
  input  C0,
  input  A0,
  input  B0,
  input  A1,
  input  B1,
  input  A2,
  input  B2,
  input  A3,
  input  B3,
  output S0,
  output S1,
  output S2,
  output S3,
  output C4
);

  wire nand_1_out, nand_2_out, nand_3_out, nand_4_out, nand_5_out, nand_6_out, nand_7_out, nand_9_out,
       nand_10_out, nand_11_out, nand_12_out, xor_1_out, xor_2_out, xor_3_out, xor_4_out;

  nand nand_1 (nand_1_out, A0, B0);
  nand nand_2 (nand_2_out, A1, B1);
  nand nand_3 (nand_3_out, A2, B2);
  nand nand_4 (nand_4_out, A3, B3);
  xor xor_1 (xor_1_out, A0, B0);
  nand nand_5 (nand_5_out, nand_1_out, nand_9_out);
  xor xor_2 (xor_2_out, A1, B1);
  nand nand_6 (nand_6_out, nand_2_out, nand_10_out);
  xor xor_3 (xor_3_out, A2, B2);
  nand nand_7 (nand_7_out, nand_3_out, nand_11_out);
  xor xor_4 (xor_4_out, A3, B3);
  nand nand_8 (C4, nand_4_out, nand_12_out);
  nand nand_9 (nand_9_out, C0, xor_1_out);
  nand nand_10 (nand_10_out, nand_5_out, xor_2_out);
  nand nand_11 (nand_11_out, nand_6_out, xor_3_out);
  nand nand_12 (nand_12_out, nand_7_out, xor_4_out);
  xor xor_5 (S0, xor_1_out, C0);
  xor xor_6 (S1, xor_2_out, nand_5_out);
  xor xor_7 (S2, xor_3_out, nand_6_out);
  xor xor_8 (S3, xor_4_out, nand_7_out);

  // Notes on the sheet:
  //   输出 = S3S2S1S0 , 以及向高位的进位C0
  //   C1
  //   C2
  //   C3
  //   串行进位二进制并行加法器
  //   输入A = A3A2A1A0 , B = B3B2B1B0 , 以及来自低位的进位C0
endmodule
