// Logisim project exp1_4.circ as structural Verilog: 1 circuit, main circuit 4位二进制超前进位加法器
module \_4位二进制超前进位加法器  (
  input  B3,
  input  A3,
  input  B2,
  input  A2,
  input  B1,
  input  A1,
  input  B0,
  input  A0,
  input  C_1,
  output C3,
  output S3,
  output S2,
  output S1,
  output S0
);

  wire and_1_out, and_2_out, and_3_out, and_4_out, and_5_out, and_6_out, and_7_out, and_8_out, and_9_out,
       and_10_out, and_11_out, and_12_out, and_13_out, and_14_out, nand_1_out, nand_2_out, nand_3_out,
       nand_4_out, nor_1_out, nor_2_out, nor_3_out, nor_4_out, nor_5_out, nor_6_out, nor_7_out, not_1_out,
       not_2_out, not_3_out, not_4_out, not_5_out, not_6_out;

  nand nand_1 (nand_1_out, B3, A3);
  nor nor_1 (nor_1_out, B3, A3);
  nand nand_2 (nand_2_out, B2, A2);
  nor nor_2 (nor_2_out, B2, A2);
  nand nand_3 (nand_3_out, B1, A1);
  nor nor_3 (nor_3_out, B1, A1);
  nand nand_4 (nand_4_out, B0, A0);
  nor nor_4 (nor_4_out, B0, A0);
  not not_1 (not_1_out, C_1);
  not not_2 (not_2_out, nor_4_out);
  and and_1 (and_1_out, nand_4_out, not_1_out);
  and and_2 (and_2_out, nand_4_out, ~nor_4_out);  // AND_Gate
  not not_3 (not_3_out, not_1_out);
  not not_4 (not_4_out, nand_1_out);
  not not_5 (not_5_out, nor_2_out);
  not not_6 (not_6_out, nor_3_out);
  and and_3 (and_3_out, nor_2_out, nand_1_out);
  and and_4 (and_4_out, nor_3_out, nand_1_out, nand_2_out);
  and and_5 (and_5_out, nor_4_out, nand_1_out, nand_2_out, nand_3_out);
  and and_6 (and_6_out, nand_1_out, nand_2_out, nand_3_out, nand_4_out, not_1_out);
  and and_7 (and_7_out, nand_1_out, ~nor_1_out);  // AND_Gate
  and and_8 (and_8_out, nor_3_out, nand_2_out);
  and and_9 (and_9_out, nor_4_out, nand_2_out, nand_3_out);
  and and_10 (and_10_out, nand_2_out, nand_3_out, nand_4_out, not_1_out);
  and and_11 (and_11_out, nand_2_out, ~nor_2_out);  // AND_Gate
  and and_12 (and_12_out, nor_4_out, nand_3_out);
  and and_13 (and_13_out, nand_3_out, nand_4_out, not_1_out);
  and and_14 (and_14_out, nand_3_out, ~nor_3_out);  // AND_Gate
  nor nor_5 (nor_5_out, not_2_out, and_1_out);
  nor nor_6 (nor_6_out, not_5_out, and_8_out, and_9_out, and_10_out);
  nor nor_7 (nor_7_out, not_6_out, and_12_out, and_13_out);
  nor nor_8 (C3, not_4_out, and_3_out, and_4_out, and_5_out, and_6_out);
  xor xor_1 (S3, and_7_out, nor_6_out);
  xor xor_2 (S2, and_11_out, nor_7_out);
  xor xor_3 (S1, and_14_out, nor_5_out);
  xor xor_4 (S0, and_2_out, not_3_out);

  // Notes on the sheet:
  //   ！P2
  //   ！P1
  //   ！P0
  //   输出 = S3S2S1S0 , 以及向高位的进位C3
  //   先行进位四位二进制并行加法器
  //   输入A = A3A2A1A0 , B = B3B2B1B0 , 以及来自低位的进位C-1
  //   K3
  //   K2
  //   K1
  //   C0
  //   C2
  //   C1
  //   K0
  //   C-1
endmodule
