// Logisim project exp1_5.circ as structural Verilog: 1 circuit, main circuit main
module main (
  input  B3,
  input  B2,
  input  B1,
  input  B0,
  input  A3,
  input  A2,
  input  A1,
  input  A0,
  input  in_9,
  output C3,
  output S3,
  output S2,
  output S1,
  output S0
);

  wire adder_1_cout, \四位二进制并行加法器_1_c3 , \四位二进制并行加法器_1_s0 , \四位二进制并行加法器_1_s1 , \四位二进制并行加法器_1_s2 ,
       \四位二进制并行加法器_1_s3 ;
  wire [3:0] adder_1_out;

  \四位二进制并行加法器  \u_四位二进制并行加法器_1  (
    .A0(B0), .B0(A0), .S0(\四位二进制并行加法器_1_s0 ), .S1(\四位二进制并行加法器_1_s1 ), .A1(B1), .B1(A1), .A2(B2), .B2(A2),
    .S2(\四位二进制并行加法器_1_s2 ), .B3(A3), .A3(B3), .S3(\四位二进制并行加法器_1_s3 ), .C3(\四位二进制并行加法器_1_c3 ), .C_1(in_9));
  Adder #(.width(4)) adder_1 (
    .a({B3, B2, B1, B0}), .b({A3, A2, A1, A0}), .out(adder_1_out), .cin(in_9), .cout(adder_1_cout));
  xor xor_1 (C3, \四位二进制并行加法器_1_c3 , adder_1_cout);
  xor xor_2 (S3, \四位二进制并行加法器_1_s3 , adder_1_out[3]);
  xor xor_3 (S2, \四位二进制并行加法器_1_s2 , adder_1_out[2]);
  xor xor_4 (S1, \四位二进制并行加法器_1_s1 , adder_1_out[1]);
  xor xor_5 (S0, \四位二进制并行加法器_1_s0 , adder_1_out[0]);
endmodule
