// Logisim project exp3_s.circ as structural Verilog: 1 circuit, main circuit main
module main (
  input  in_1,
  input  in_2
);

  exp1_3_main main_1 (.A0(in_1), .A1(in_2));  // open: B0, B1, A2, B2, A3, B3, S0, S1, S2, S3, C4, C0
endmodule
