// Logisim project exp2_1.circ as structural Verilog: 1 circuit, main circuit main
module main (
  output out_1,
  output out_2,
  output out_3,
  output out_4
);

  wire CLR_out, CPD_out, CPU_out;

  Button CPU (.out(CPU_out));
  Button CLR (.out(CLR_out));
  Button CPD (.out(CPD_out));
  exp2_1_lib_main main_1 (.CPU(CPU_out), .CLR(CLR_out), .CLD(CPD_out), .SA(out_4), .SB(out_3), .SC(out_2), .SD(out_1));
endmodule
