// Logisim project exp2_1_lib.circ as structural Verilog: 1 circuit, main circuit main
// 四位二进制可逆计数器
module main (
  input  CPU,
  input  CLR,
  input  CLD,
  output SA,
  output SB,
  output SC,
  output SD
);

  wire d_ff_1_qn, d_ff_2_qn, d_ff_3_qn, d_ff_4_qn, or_1_out, xor_1_out, xor_2_out, xor_3_out;

  or or_1 (or_1_out, CPU, CLD);
  D_Flip_Flop d_ff_1 (.clk(or_1_out), .D(d_ff_1_qn), .Q(SA), .Qn(d_ff_1_qn), .reset(CLR));  // open: preset, en
  xor xor_1 (xor_1_out, d_ff_1_qn, CLD);
  D_Flip_Flop d_ff_2 (.clk(xor_1_out), .D(d_ff_2_qn), .Q(SB), .Qn(d_ff_2_qn), .reset(CLR));  // open: preset, en
  xor xor_2 (xor_2_out, d_ff_2_qn, CLD);
  D_Flip_Flop d_ff_3 (.clk(xor_2_out), .D(d_ff_3_qn), .Q(SC), .Qn(d_ff_3_qn), .reset(CLR));  // open: preset, en
  xor xor_3 (xor_3_out, d_ff_3_qn, CLD);
  D_Flip_Flop d_ff_4 (.clk(xor_3_out), .D(d_ff_4_qn), .Q(SD), .Qn(d_ff_4_qn), .reset(CLR));  // open: preset, en
endmodule
