// Logisim project exp2_2_lib.circ as structural Verilog: 1 circuit, main circuit main
// 2进制8421转换器
module main (
  input  I3,
  input  I2,
  input  I1,
  input  I0,
  output S7,
  output S6,
  output S5,
  output S4,
  output S3,
  output S2,
  output S1,
  output S0
);

  wire or_1_out;

  \四位二进制并行加法器  \u_四位二进制并行加法器_1  (
    .A0(I0), .B0(1'b0), .S0(S0), .S1(S1), .A1(I1), .B1(S4), .A2(I2), .B2(S4), .S2(S2), .B3(1'b0), .A3(I3),
    .S3(S3), .C_1(1'b0));  // open: C3
  or or_1 (or_1_out, I2, I1);
  and and_1 (S4, I3, or_1_out);

  assign S5 = 1'b0;
  assign S6 = 1'b0;
  assign S7 = 1'b0;
endmodule
