// Logisim project exp2_3.circ as structural Verilog: 1 circuit, main circuit main
// 2位7段译码器
module main (
  input  I7,
  input  I6,
  input  I5,
  input  I4,
  input  I3,
  input  I2,
  input  I1,
  input  I0,
  output a,
  output b,
  output c,
  output d,
  output e,
  output f,
  output g,
  output a_2,
  output b_2,
  output c_2,
  output d_2,
  output e_2,
  output f_2,
  output g_2
);

  exp2_3_lib_main main_1 (.A3(I7), .A2(I6), .A1(I5), .A0(I4), .Fa(a), .Fb(b), .Fc(c), .Fd(d), .Fe(e), .Ff(f), .Fg(g));
  _7_Segment_Display u_7_segment_display_1 (.g(g), .f(f), .a(a), .b(b), .e(e), .d(d), .c(c));  // open: dp
  exp2_3_lib_main main_2 (
    .A3(I3), .A2(I2), .A1(I1), .A0(I0), .Fa(a_2), .Fb(b_2), .Fc(c_2), .Fd(d_2), .Fe(e_2), .Ff(f_2), .Fg(g_2));
  _7_Segment_Display u_7_segment_display_2 (.g(g_2), .f(f_2), .a(a_2), .b(b_2), .e(e_2), .d(d_2), .c(c_2));  // open: dp
endmodule
