// Logisim project exp2_4.circ as structural Verilog: 1 circuit, main circuit main
// 门禁可逆计数器
module main (
  input  in_1,
  input  in_2,
  input  in_3,
  output \门禁 ,
  output SD,
  output SC,
  output SB,
  output SA
);

  wire and_1_out, and_2_out, CLR_out, CPD_out, CPU_out, nand_1_out, not_1_out, or_1_out, or_2_out, or_3_out,
       or_4_out;

  Button CPU (.out(CPU_out));
  Button CLR (.out(CLR_out));
  Button CPD (.out(CPD_out));
  or or_1 (or_1_out, CPU_out, in_1);
  or or_2 (or_2_out, CLR_out, in_2);
  or or_3 (or_3_out, CPD_out, in_3);
  not not_1 (not_1_out, nand_1_out);
  and and_1 (and_1_out, nand_1_out, or_1_out);
  and and_2 (and_2_out, or_4_out, or_3_out);
  and and_3 (\门禁 , not_1_out, or_1_out);
  LED led_1 (.in(\门禁 ));
  nand nand_1 (nand_1_out, SD, SC, SB, SA);
  or or_4 (or_4_out, SD, SC, SB, SA);
  exp2_1_lib_main main_1 (.CPU(and_1_out), .CLR(or_2_out), .CLD(and_2_out), .SA(SA), .SB(SB), .SC(SC), .SD(SD));

  // Notes on the sheet:
  //   警告！
endmodule
