// Logisim project exp2_5.circ as structural Verilog: 1 circuit, main circuit main
module main (
);

  wire CLR_out, CPD_out, CPU_out, main_1_a, main_1_a_2, main_1_b, main_1_b_2, main_1_c, main_1_c_2, main_1_d,
       main_1_d_2, main_1_e, main_1_e_2, main_1_f, main_1_f_2, main_1_g, main_1_g_2, main_1_w;

  Button CPU (.out(CPU_out));
  Button CLR (.out(CLR_out));
  Button CPD (.out(CPD_out));
  _7_Segment_Display u_7_segment_display_1 (
    .g(main_1_g), .f(main_1_f), .a(main_1_a), .b(main_1_b), .e(main_1_e), .d(main_1_d), .c(main_1_c));  // open: dp
  _7_Segment_Display u_7_segment_display_2 (
    .g(main_1_g_2), .f(main_1_f_2), .a(main_1_a_2), .b(main_1_b_2), .e(main_1_e_2), .d(main_1_d_2),
    .c(main_1_c_2));  // open: dp
  LED led_1 (.in(main_1_w));
  exp2_5_lib_main main_1 (
    .CPU(CPU_out), .CLR(CLR_out), .CPD(CPD_out), .W(main_1_w), .a(main_1_a), .b(main_1_b), .c(main_1_c),
    .d(main_1_d), .e(main_1_e), .f(main_1_f), .g(main_1_g), .a_2(main_1_a_2), .b_2(main_1_b_2),
    .c_2(main_1_c_2), .d_2(main_1_d_2), .e_2(main_1_e_2), .f_2(main_1_f_2), .g_2(main_1_g_2));
endmodule
