// Logisim project exp2_5_lib.circ as structural Verilog: 1 circuit, main circuit main
// 封装后的门禁系统逻辑符号
module main (
  input  CPU,
  input  CLR,
  input  CPD,
  output a,
  output b,
  output c,
  output d,
  output e,
  output f,
  output g,
  output a_2,
  output b_2,
  output c_2,
  output d_2,
  output e_2,
  output f_2,
  output g_2,
  output W
);

  wire main_1_s0, main_1_s1, main_1_s2, main_1_s3, main_1_s4, main_1_s5, main_1_s6, main_1_s7, main_2_sa,
       main_2_sb, main_2_sc, main_2_sd;

  exp2_2_lib_main main_1 (
    .S4(main_1_s4), .S3(main_1_s3), .S2(main_1_s2), .S1(main_1_s1), .S0(main_1_s0), .I3(main_2_sd),
    .I2(main_2_sc), .I1(main_2_sb), .I0(main_2_sa), .S5(main_1_s5), .S6(main_1_s6), .S7(main_1_s7));
  exp2_4_main main_2 (
    .in_1(CPU), .in_2(CLR), .in_3(CPD), .\门禁 (W), .SD(main_2_sd), .SC(main_2_sc), .SB(main_2_sb),
    .SA(main_2_sa));
  exp2_3_main main_3 (
    .I7(main_1_s7), .I6(main_1_s6), .I5(main_1_s5), .I4(main_1_s4), .I3(main_1_s3), .I2(main_1_s2),
    .I1(main_1_s1), .I0(main_1_s0), .a(a), .b(b), .c(c), .d(d), .e(e), .f(f), .g(g), .a_2(a_2), .b_2(b_2),
    .c_2(c_2), .d_2(d_2), .e_2(e_2), .f_2(f_2), .g_2(g_2));
endmodule
